# Fritzing sketch skema JOB3 (saved by Fritzing 0.9.3b)
breadboards: 1
stripboards: 3

parts:
  WeMos_D1_R1 = WeMos D1 R2
  LCD1 = LCD screen  # not connected
  Part1 = RFID-RC522-v3

nets:
  N1: WeMos_D1_R1.(D5), Part1.SCK
  N2: WeMos_D1_R1.(D6), Part1.MISO
  N3: WeMos_D1_R1.(D7), Part1.MOSI
  N4: WeMos_D1_R1.D9, Part1.RST
  N5: WeMos_D1_R1.D10, Part1.SDA

notes:
  5V
  3,3V
  LCD+I2C
  GND
  SDA
  SCL
  SS/SDA
  SCK
  MISO
  MOSI
  RST
  Ext power
  RELAY
  BUZZER
  CH1
  VCC

custom parts:
  WeMos D1 R2: The D1 R2 is a mini wifi board based on the ESP-8266EX.
  RFID-RC522-v3: A simple China made RFID-RC522 Reader (6x4 cm); do check the pin labels, as this is a MFRC522 based clone.
