# Fritzing sketch skema ldr lcd (saved by Fritzing 0.9.3b)
breadboards: 1
stripboards: 2

parts:
  LCD1 = LCD screen  # not connected
  R1 = Photocell (LDR) [package=THT]
  R2 = Resistor [tolerance=±5% resistance=220 package=THT]
  U1 = NodeMCU V3.0

nets:
  N1: R1.pin_0, U1.Vin
  N2: R1.pin_1, R2.Pin_1, U1.A0

notes:
  5V
  3,3V
  LCD+I2C
  GND
  SDA
  SCL
  Ext power
  OUT
  LDR

custom parts:
  NodeMCU V3.0: ESP8266 based NodeMCU
