# Fritzing sketch skema (saved by Fritzing 0.9.3b)
breadboards: 1
stripboards: 1

parts:
  WeMos_D1_R1 = WeMos D1 R2
  LCD1 = LCD screen  # not connected
  R1 = Photocell (LDR) [package=THT]

nets:
  N1: WeMos_D1_R1.A0, R1.pin_1
  N2: WeMos_D1_R1.VIN, R1.pin_0

notes:
  5V
  3,3V
  LCD+I2C
  VCC
  GND
  SDA
  SCL

custom parts:
  WeMos D1 R2: The D1 R2 is a mini wifi board based on the ESP-8266EX.
